# Fritzing sketch raspberry-pi-sketch (saved by Fritzing 0.8.3b)
breadboards: 1

parts:
  R1 = Resistor [tolerance=±5% resistance=220 package=THT]
  LED1 = LED - 5mm [color="Red (633nm)" package="5 mm [THT]"]
  Raspberry_Pi_rev1 = Raspberry Pi rev1

nets:
  N1: R1.Pin_0, Raspberry_Pi_rev1.GPIO_23
  N2: R1.Pin_1, LED1.anode
  N3: LED1.cathode, Raspberry_Pi_rev1.GND
